# Fritzing sketch Drum (saved by Fritzing 0.9.4)
breadboards: 1

parts:
  SOM1 = Daisy Seed [chip_label=IC package="DIP (Dual Inline) [THT]"]
  SPKR1 = Loudspeaker
  S1 = Pushbutton [package="[THT]"]
  S2 = Pushbutton [package="[THT]"]

nets:
  N1: SOM1.pin_19, SPKR1.pin2
  GND: SOM1.pin_20, SOM1.pin_40, SPKR1.pin1, S1.Pin_1, S1.Pin_2, S2.Pin_1, S2.Pin_2
  N2: SOM1.pin_34, S1.Pin_3, S1.Pin_4
  N3: SOM1.pin_35, S2.Pin_3, S2.Pin_4

custom parts:
  Daisy Seed: Daisy is an embedded platform for music. It features everything you need for creating high fidelity audio hardware devices. Just plug in a USB cable and start making sound! No soldering required.
