# Fritzing sketch Knob (saved by Fritzing 0.9.6b)
breadboards: 1

parts:
  SOM1 = Daisy Seed [chip_label=IC package="DIP (Dual Inline) [THT]"]
  R1 = Rotary Potentiometer (Small) [maximum_resistance=100kΩ package=THT]
  R2 = Resistor [tolerance=±5% power=0.25 resistance=220 package=THT]
  LED1 = LED - 5mm [color="Red (633nm)" current=0.030 package="5 mm [THT]"]

nets:
  GND: SOM1.pin_20, SOM1.pin_40, R1.leg1, LED1.cathode
  N1: SOM1.pin_21, R1.leg2
  N2: SOM1.pin_28, R1.wiper
  N3: SOM1.pin_35, R2.Pin_1
  N4: R2.Pin_0, LED1.anode

custom parts:
  Daisy Seed: Daisy is an embedded platform for music. It features everything you need for creating high fidelity audio hardware devices. Just plug in a USB cable and start making sound! No soldering required.
