# Fritzing sketch SeedButton (saved by Fritzing 0.9.4)
breadboards: 1

parts:
  S1 = Pushbutton [package="[THT]"]
  SOM1 = Daisy Seed [chip_label=IC package="DIP (Dual Inline) [THT]"]

nets:
  N1: S1.Pin_1, S1.Pin_2, SOM1.pin_35
  GND: S1.Pin_3, S1.Pin_4, SOM1.pin_20, SOM1.pin_40

custom parts:
  Daisy Seed: Daisy is an embedded platform for music. It features everything you need for creating high fidelity audio hardware devices. Just plug in a USB cable and start making sound! No soldering required.
