# Fritzing sketch SeedKnob (saved by Fritzing 0.9.4)
breadboards: 1

parts:
  SOM1 = Daisy Seed [chip_label=IC package="DIP (Dual Inline) [THT]"]
  R1 = Resistor [tolerance=±5% resistance=1k package=THT]
  LED1 = LED - 5mm [color="Red (633nm)" package="5 mm [THT]"]
  R2 = Rotary Potentiometer (Small) [maximum_resistance=100kΩ package=THT]

nets:
  GND: SOM1.pin_20, SOM1.pin_40, LED1.cathode, R2.leg1
  3.3V: SOM1.pin_21, R2.leg2
  N1: SOM1.pin_28, R2.wiper
  N2: SOM1.pin_35, R1.Pin_0
  N3: R1.Pin_1, LED1.anode

custom parts:
  Daisy Seed: Daisy is an embedded platform for music. It features everything you need for creating high fidelity audio hardware devices. Just plug in a USB cable and start making sound! No soldering required.
